// Logisim project Final_Circuit.circ as structural Verilog: 1 circuit, main circuit Final
module Final (
);

  wire and_1_out, and_2_out, and_6_out, and_7_out, and_8_out, and_10_out, and_11_out, CLK, CLK_Stopwatch,
       clock_1_out, Counter_H0_p7, Counter_H1_p1, Counter_H1_p2, Counter_H1_p9, Counter_M0_p1,
       Counter_M0_p14, Counter_M1_p1, Counter_M1_p13, Counter_M1_p14, Counter_S1_p1, Counter_S1_p13,
       Counter_S1_p14, Display_H0_p1, Display_H0_p2, Display_H0_p4, Display_H0_p5, Display_H0_p6,
       Display_H0_p7, Display_H0_p8, Display_H0_p9, Display_H0_p10, Display_H0_p11, Display_H1_p2,
       Display_H1_p3, Display_H1_p4, Display_H1_p5, Display_H1_p6, Display_H1_p7, Display_H1_p8,
       Display_H1_p9, Display_H1_p10, Display_H1_p11, Display_M0_p1, Display_M0_p2, Display_M0_p3,
       Display_M0_p4, Display_M0_p5, Display_M0_p6, Display_M0_p7, Display_M0_p8, Display_M0_p9,
       Display_M0_p10, Display_M0_p11, Display_M1_p1, Display_M1_p2, Display_M1_p3, Display_M1_p4,
       Display_M1_p5, Display_M1_p6, Display_M1_p7, Display_M1_p8, Display_M1_p9, Display_M1_p10,
       Display_M1_p11, Display_S0_p1, Display_S0_p2, Display_S0_p3, Display_S0_p4, Display_S0_p5,
       Display_S0_p6, Display_S0_p7, Display_S0_p8, Display_S0_p9, Display_S0_p10, Display_S0_p11,
       Display_S1_p1, Display_S1_p2, Display_S1_p3, Display_S1_p4, Display_S1_p5, Display_S1_p6,
       Display_S1_p7, Display_S1_p8, Display_S1_p9, Display_S1_p10, Display_S1_p11, H0_4, H1_2,
       Manual_Reset_Clock, MUX_H0_p3, MUX_H0_p4, MUX_H0_p9, MUX_H0_p10, MUX_H1_p4, MUX_H1_p5, MUX_H1_p10,
       MUX_H1_p11, MUX_M0_p3, MUX_M0_p4, MUX_M0_p5, MUX_M0_p6, MUX_M0_p9, MUX_M0_p10, MUX_M0_p11, MUX_M0_p12,
       MUX_M1_p3, MUX_M1_p4, MUX_M1_p5, MUX_M1_p6, MUX_M1_p9, MUX_M1_p10, MUX_M1_p11, MUX_M1_p12, MUX_S0_p3,
       MUX_S0_p4, MUX_S0_p5, MUX_S0_p6, MUX_S0_p9, MUX_S0_p10, MUX_S0_p11, MUX_S0_p12, MUX_S1_p3, MUX_S1_p4,
       MUX_S1_p5, MUX_S1_p6, MUX_S1_p9, MUX_S1_p10, MUX_S1_p11, MUX_S1_p12, nor_1_out, not_1_out, not_2_out,
       not_3_out, not_4_out, not_5_out, not_6_out, not_7_out, not_8_out, or_2_out, or_4_out, Pause_Clock,
       Pause_Stopwatch, Reset, Reset_Stopwatch, Stopwatch_Mode, Time_Set, UP_H0, UP_M0;

  Clock clock_1 (.out(clock_1_out));
  not not_1 (not_1_out, Time_Set);
  _7_Segment_Display #(.active("false"), .decimalPoint("false")) H1 (
    .g(Display_H1_p4), .f(Display_H1_p2), .a(Display_H1_p5), .b(Display_H1_p6), .e(Display_H1_p11),
    .d(Display_H1_p9), .c(Display_H1_p7));
  // cd4511 Display_H1: pin names not known; wires that end beside it: H1_2, Display_H1_p2, Display_H1_p3, Display_H1_p4, Display_H1_p5, Display_H1_p6, Display_H1_p7, Display_H1_p8, Display_H1_p9, Display_H1_p10, Display_H1_p11
  // cmos_74HC157 MUX_H1: pin names not known; wires that end beside it: Stopwatch_Mode, Stopwatch_Mode, 1'b0, MUX_H1_p4, MUX_H1_p5, 1'b0, 1'b0, Display_H1_p10, Display_H1_p8, MUX_H1_p10, MUX_H1_p11, 1'b0, 1'b0, H1_2, Display_H1_p3
  // cd4518 Counter_H1: pin names not known; wires that end beside it: Counter_H1_p1, Counter_H1_p2, Counter_H1_p1, MUX_H1_p5, MUX_H1_p11, MUX_H1_p10, MUX_H1_p4, 1'b1, Counter_H1_p9
  and and_1 (and_1_out, not_1_out, clock_1_out);
  or or_1 (Counter_H1_p9, Counter_H1_p1, nor_1_out);
  not not_2 (not_2_out, Pause_Clock);
  and and_2 (and_2_out, Stopwatch_Mode, and_1_out);
  and and_3 (CLK, and_1_out, not_2_out);
  nor nor_1 (nor_1_out, MUX_H0_p3, MUX_H0_p9, MUX_H0_p10, MUX_H0_p4);
  not not_3 (not_3_out, Pause_Stopwatch);
  and and_4 (CLK_Stopwatch, and_2_out, not_3_out);
  // cd4511 Display_H0: pin names not known; wires that end beside it: Display_H0_p1, Display_H0_p2, H0_4, Display_H0_p4, Display_H0_p5, Display_H0_p6, Display_H0_p7, Display_H0_p8, Display_H0_p9, Display_H0_p10, Display_H0_p11
  // cmos_74HC157 MUX_H0: pin names not known; wires that end beside it: Stopwatch_Mode, 1'b0, MUX_H0_p3, MUX_H0_p4, 1'b0, 1'b0, Display_H0_p10, Display_H0_p8, MUX_H0_p9, MUX_H0_p10, 1'b0, 1'b0, Display_H0_p1, H0_4
  // cd4518 Counter_H0: pin names not known; wires that end beside it: Counter_H1_p1, MUX_H0_p4, MUX_H0_p10, MUX_H0_p9, MUX_H0_p3, 1'b1, Counter_H0_p7
  _7_Segment_Display #(.active("false"), .decimalPoint("false")) H0 (
    .g(Display_H0_p4), .f(Display_H0_p2), .a(Display_H0_p5), .b(Display_H0_p6), .e(Display_H0_p11),
    .d(Display_H0_p9), .c(Display_H0_p7));
  and and_5 (Counter_H0_p7, not_4_out, not_5_out);
  not not_4 (not_4_out, and_7_out);
  not not_5 (not_5_out, and_6_out);
  and and_6 (and_6_out, UP_H0, Time_Set);
  and and_7 (and_7_out, MUX_M1_p10, MUX_M1_p9);
  _7_Segment_Display #(.active("false"), .decimalPoint("false")) M1 (
    .g(Display_M1_p4), .f(Display_M1_p2), .a(Display_M1_p5), .b(Display_M1_p6), .e(Display_M1_p11),
    .d(Display_M1_p9), .c(Display_M1_p7));
  // cd4511 Display_M1: pin names not known; wires that end beside it: Display_M1_p1, Display_M1_p2, Display_M1_p3, Display_M1_p4, Display_M1_p5, Display_M1_p6, Display_M1_p7, Display_M1_p8, Display_M1_p9, Display_M1_p10, Display_M1_p11
  // cmos_74HC157 MUX_M1: pin names not known; wires that end beside it: Stopwatch_Mode, 1'b0, MUX_M1_p3, MUX_M1_p4, MUX_M1_p5, MUX_M1_p6, Display_M1_p10, Display_M1_p8, MUX_M1_p9, MUX_M1_p10, MUX_M1_p11, MUX_M1_p12, Display_M1_p1, Display_M1_p3
  or or_2 (or_2_out, Counter_H1_p1, and_7_out);
  // cd4518 Counter_M1: pin names not known; wires that end beside it: Counter_M1_p1, or_2_out, 1'b1, MUX_M1_p4, MUX_M1_p5, MUX_M1_p10, MUX_M1_p11, MUX_M1_p9, MUX_M1_p12, MUX_M1_p3, MUX_M1_p6, 1'b1, Counter_M1_p13, Counter_M1_p14
  or or_3 (Counter_M1_p13, Counter_H1_p2, and_8_out);
  and and_8 (and_8_out, MUX_M1_p12, MUX_M1_p11);
  Button u_UP_H0 (.out(UP_H0));
  nor nor_2 (Counter_M1_p14, MUX_M0_p3, MUX_M0_p9, MUX_M0_p10, MUX_M0_p4);
  nor nor_3 (Counter_M1_p1, MUX_M0_p5, MUX_M0_p11, MUX_M0_p12, MUX_M0_p6);
  Button u_UP_M0 (.out(UP_M0));
  // cd4511 Display_M0: pin names not known; wires that end beside it: Display_M0_p1, Display_M0_p2, Display_M0_p3, Display_M0_p4, Display_M0_p5, Display_M0_p6, Display_M0_p7, Display_M0_p8, Display_M0_p9, Display_M0_p10, Display_M0_p11
  // cmos_74HC157 MUX_M0: pin names not known; wires that end beside it: Stopwatch_Mode, 1'b0, MUX_M0_p3, MUX_M0_p4, MUX_M0_p5, MUX_M0_p6, Display_M0_p10, Display_M0_p8, MUX_M0_p9, MUX_M0_p10, MUX_M0_p11, MUX_M0_p12, Display_M0_p1, Display_M0_p3
  // cd4518 Counter_M0: pin names not known; wires that end beside it: Counter_M0_p1, Counter_H1_p1, 1'b1, MUX_M0_p4, MUX_M0_p5, MUX_M0_p10, MUX_M0_p11, MUX_M0_p9, MUX_M0_p12, MUX_M0_p3, MUX_M0_p6, 1'b1, Counter_H1_p2, Counter_M0_p14
  _7_Segment_Display #(.active("false"), .decimalPoint("false")) M0 (
    .g(Display_M0_p4), .f(Display_M0_p2), .a(Display_M0_p5), .b(Display_M0_p6), .e(Display_M0_p11),
    .d(Display_M0_p9), .c(Display_M0_p7));
  and and_9 (Counter_M0_p14, not_7_out, not_6_out);
  not not_6 (not_6_out, and_10_out);
  not not_7 (not_7_out, and_11_out);
  and and_10 (and_10_out, UP_M0, Time_Set);
  and and_11 (and_11_out, MUX_S1_p10, MUX_S1_p9);
  _7_Segment_Display #(.active("false"), .decimalPoint("false")) S1 (
    .g(Display_S1_p4), .f(Display_S1_p2), .a(Display_S1_p5), .b(Display_S1_p6), .e(Display_S1_p11),
    .d(Display_S1_p9), .c(Display_S1_p7));
  // cd4511 Display_S1: pin names not known; wires that end beside it: Display_S1_p1, Display_S1_p2, Display_S1_p3, Display_S1_p4, Display_S1_p5, Display_S1_p6, Display_S1_p7, Display_S1_p8, Display_S1_p9, Display_S1_p10, Display_S1_p11
  // cmos_74HC157 MUX_S1: pin names not known; wires that end beside it: Stopwatch_Mode, 1'b0, MUX_S1_p3, MUX_S1_p4, MUX_S1_p5, MUX_S1_p6, Display_S1_p10, Display_S1_p8, MUX_S1_p9, MUX_S1_p10, MUX_S1_p11, MUX_S1_p12, Display_S1_p1, Display_S1_p3
  or or_4 (or_4_out, Counter_H1_p1, and_11_out);
  // cd4518 Counter_S1: pin names not known; wires that end beside it: Counter_S1_p1, or_4_out, 1'b1, MUX_S1_p4, MUX_S1_p5, MUX_S1_p10, MUX_S1_p11, MUX_S1_p9, MUX_S1_p12, MUX_S1_p3, MUX_S1_p6, 1'b1, Counter_S1_p13, Counter_S1_p14
  or or_5 (Counter_S1_p13, Counter_H1_p2, Counter_M0_p1);
  and and_12 (Counter_M0_p1, MUX_S1_p12, MUX_S1_p11);
  DipSwitch #(.number(6)) dipswitch_1 (
    .sw1(Pause_Clock), .sw2(Manual_Reset_Clock), .sw3(Stopwatch_Mode), .sw4(Pause_Stopwatch),
    .sw5(Reset_Stopwatch), .sw6(Time_Set));
  nor nor_4 (Counter_S1_p14, MUX_S0_p3, MUX_S0_p9, MUX_S0_p10, MUX_S0_p4);
  nor nor_5 (Counter_S1_p1, MUX_S0_p5, MUX_S0_p11, MUX_S0_p12, MUX_S0_p6);
  // cd4511 Display_S0: pin names not known; wires that end beside it: Display_S0_p1, Display_S0_p2, Display_S0_p3, Display_S0_p4, Display_S0_p5, Display_S0_p6, Display_S0_p7, Display_S0_p8, Display_S0_p9, Display_S0_p10, Display_S0_p11
  // cmos_74HC157 MUX_S0: pin names not known; wires that end beside it: Stopwatch_Mode, 1'b0, MUX_S0_p3, MUX_S0_p4, MUX_S0_p5, MUX_S0_p6, Display_S0_p10, Display_S0_p8, MUX_S0_p9, MUX_S0_p10, MUX_S0_p11, MUX_S0_p12, Display_S0_p1, Display_S0_p3
  // cd4518 Counter_S0: pin names not known; wires that end beside it: CLK_Stopwatch, Counter_H1_p1, 1'b1, MUX_S0_p4, MUX_S0_p5, MUX_S0_p10, MUX_S0_p11, MUX_S0_p9, MUX_S0_p12, MUX_S0_p3, MUX_S0_p6, 1'b1, Counter_H1_p2, CLK
  _7_Segment_Display #(.active("false"), .decimalPoint("false")) SO (
    .g(Display_S0_p4), .f(Display_S0_p2), .a(Display_S0_p5), .b(Display_S0_p6), .e(Display_S0_p11),
    .d(Display_S0_p9), .c(Display_S0_p7));
  or or_6 (Counter_H1_p2, not_8_out, Reset_Stopwatch);
  or or_7 (Counter_H1_p1, Reset, Manual_Reset_Clock);
  not not_8 (not_8_out, Stopwatch_Mode);
  and and_13 (Reset, H1_2, H0_4);

  // Notes on the sheet:
  //   Digital Clock H1
  //   Hours
  //   Time Set | Pause Digital Clock | Start & Pause Stopwatch
  //   Digital Clock H0
  //   :
  //   Digital Clock M1
  //   Stopwatch M1
  //   Minutes
  //   Time Set Features
  //   24-Hour Digital Clock (HH:MM:SS) & Stopwatch (MM:SS)
  //   Digital Clock M0
  //   Stopwatch M0
  //   :
  //   Digital Clock S1
  //   Stopwatch S1
  //   DIP Switch
  //   Seconds
  //   Digital Clock S0
  //   Stopwatch S0
  //   Reset at 24:00:00
endmodule
