// Logisim project Final_Project_Circuit.circ as structural Verilog
module main (
  input  in_1
);

  wire A_H1, and_1_out, and_3_out, and_4_out, and_5_out, and_7_out, and_9_out, and_10_out, B_H0, B_H1, C_H0,
       CLK, CLK_Stopwatch, clock_2_out, D_H1, E_H1, F_H0, G_H0, G_H1, H0_4, H0_4_out, H0_Count_0_9_pin3,
       H0_Count_0_9_pin9, H0_Count_0_9_pin10, H0_Count_0_9_pin11, H0_Count_0_9_pin12, H0_Count_0_9_pin13,
       H0_Count_0_9_pin14, H0_Count_0_9_pin15, H0_Counter_carry, H1_2, H1_2_out, H1_Count_0_2_pin3,
       H1_Count_0_2_pin9, H1_Count_0_2_pin10, H1_Count_0_2_pin11, H1_Count_0_2_pin12, H1_Count_0_2_pin13,
       H1_Count_0_2_pin14, H1_Count_0_2_pin15, M0_Stopwatch_Counter_carry, M1_Count_0_5_pin3,
       M1_Count_0_5_pin9, M1_Count_0_5_pin10, M1_Count_0_5_pin11, M1_Count_0_5_pin12, M1_Count_0_5_pin13,
       M1_Count_0_5_pin14, M1_Count_0_5_pin15, M1_Counter_carry, Manual_Reset_Clock, MO_Count_0_9_pin3,
       MO_Count_0_9_pin9, MO_Count_0_9_pin10, MO_Count_0_9_pin11, MO_Count_0_9_pin12, MO_Count_0_9_pin13,
       MO_Count_0_9_pin14, MO_Count_0_9_pin15, MO_Counter_carry, not_1_out, not_2_out, not_3_out, not_4_out,
       not_5_out, not_6_out, not_7_out, not_8_out, not_9_out, not_10_out, not_11_out, not_12_out, not_13_out,
       not_14_out, not_15_out, not_16_out, not_17_out, not_18_out, not_19_out, not_20_out, not_21_out,
       not_22_out, not_23_out, or_1_out, or_2_out, Pause_Clock, Pause_Stopwatch, Reset, Reset_Stopwatch,
       S0_Count_0_9_pin3, S0_Count_0_9_pin9, S0_Count_0_9_pin10, S0_Count_0_9_pin11, S0_Count_0_9_pin12,
       S0_Count_0_9_pin13, S0_Count_0_9_pin14, S0_Count_0_9_pin15, S0_Counter_carry,
       S0_Stopwatch_Counter_carry, S1_Count_0_5_pin3, S1_Count_0_5_pin9, S1_Count_0_5_pin10,
       S1_Count_0_5_pin11, S1_Count_0_5_pin12, S1_Count_0_5_pin13, S1_Count_0_5_pin14, S1_Count_0_5_pin15,
       S1_Counter_carry, S1_Stopwatch_Counter_carry, Stopwatch_Mode, Time_Set, UP_H0, UP_M0;
  wire [3:0] H0_Clk_Out, H0_Input, H1_Clk_Out, H1_Input, M0_Clk_Out, M0_Input, M0_Stopwatch_Counter_q,
       M1_Clk_Out, M1_Input, M1_Stopwatch_Counter_q, S0_Clk_Out, S0_Input, S0_Stopwatch_Counter_q,
       S1_Clk_Out, S1_Input, S1_Stopwatch_Counter_q;

  Counter counter_1 ();  // open: clr, load, up, count, clk, D, carry, Q
  _7447 #(.ShowInternalStructure("true")) u_7447_1 ();  // open: pin1, pin2, pin3, pin4, pin5, pin6, pin7, pin15, pin14, pin13, pin12, pin11, pin10, pin9
  Clock clock_1 ();  // open: out
  D_Flip_Flop d_ff_1 ();  // open: D, clk, Q, Qn, preset, reset
  not not_1 (not_1_out, B_H0);
  not not_2 (not_2_out, C_H0);
  not not_3 (not_3_out, G_H0);
  not not_4 (not_4_out, F_H0);
  not not_5 (not_5_out, A_H1);
  not not_6 (not_6_out, B_H1);
  not not_7 (not_7_out, D_H1);
  not not_8 (not_8_out, E_H1);
  not not_9 (not_9_out, G_H1);
  Multiplexer multiplexer_1 ();  // open: in0, in1, out, sel
  and u_H0_4 (H0_4_out, not_1_out, not_2_out, not_3_out, not_4_out);
  and and_1 (and_1_out, not_6_out, not_7_out, not_8_out, not_9_out);
  and u_H1_2 (H1_2_out, not_5_out, and_1_out);
  // AND_Gate H_24 has open pins: in0=H0_4_out, in1=H1_2_out, out=open
  and and_2 (Reset, H1_2, H0_4);
  not not_10 (not_10_out, Stopwatch_Mode);
  or or_1 (or_1_out, Reset, Manual_Reset_Clock);
  or or_2 (or_2_out, not_10_out, Reset_Stopwatch);
  _7447 #(.ShowInternalStructure("true")) H1_Count_0_2 (
    .pin1(H1_2), .pin2(H1_Input[2]), .pin3(H1_Count_0_2_pin3), .pin5(H1_Count_0_2_pin3), .pin6(H1_Input[3]),
    .pin7(H1_Input[0]), .pin15(H1_Count_0_2_pin15), .pin14(H1_Count_0_2_pin14), .pin13(H1_Count_0_2_pin13),
    .pin12(H1_Count_0_2_pin12), .pin11(H1_Count_0_2_pin11), .pin10(H1_Count_0_2_pin10),
    .pin9(H1_Count_0_2_pin9));  // open: pin4
  Counter #(.max('h2), .width(4)) H1_Counter (
    .clr(or_1_out), .clk(not_14_out), .Q(H1_Clk_Out));  // open: load, up, count, D, carry
  Clock clock_2 (.out(clock_2_out));
  Multiplexer #(.width(4)) multiplexer_2 (
    .in0(H1_Clk_Out), .in1(4'b0000), .out({H1_Input[3:2], H1_2, H1_Input[0]}), .sel(Stopwatch_Mode));
  _7_Segment_Display #(.active("false"), .decimalPoint("false")) H1 (
    .g(H1_Count_0_2_pin14), .f(H1_Count_0_2_pin15), .a(H1_Count_0_2_pin13), .b(H1_Count_0_2_pin12),
    .e(H1_Count_0_2_pin9), .d(H1_Count_0_2_pin10), .c(H1_Count_0_2_pin11));
  not not_11 (not_11_out, Time_Set);
  and and_3 (and_3_out, not_11_out, clock_2_out);
  Counter #(.max('h9), .width(4)) H0_Counter (
    .clr(or_1_out), .clk(and_4_out), .carry(H0_Counter_carry), .Q(H0_Clk_Out));  // open: load, up, count, D
  and and_4 (and_4_out, not_16_out, not_13_out);
  not not_12 (not_12_out, Pause_Clock);
  Multiplexer #(.width(4)) multiplexer_3 (
    .in0(H0_Clk_Out), .in1(4'b0000), .out({H0_Input[3], H0_4, H0_Input[1:0]}), .sel(Stopwatch_Mode));
  _7447 #(.ShowInternalStructure("true")) H0_Count_0_9 (
    .pin1(H0_Input[1]), .pin2(H0_4), .pin3(H0_Count_0_9_pin3), .pin4(H0_Count_0_9_pin3),
    .pin5(H0_Count_0_9_pin3), .pin6(H0_Input[3]), .pin7(H0_Input[0]), .pin15(H0_Count_0_9_pin15),
    .pin14(H0_Count_0_9_pin14), .pin13(H0_Count_0_9_pin13), .pin12(H0_Count_0_9_pin12),
    .pin11(H0_Count_0_9_pin11), .pin10(H0_Count_0_9_pin10), .pin9(H0_Count_0_9_pin9));
  not not_13 (not_13_out, and_7_out);
  and and_5 (and_5_out, Stopwatch_Mode, and_3_out);
  and and_6 (CLK, and_3_out, not_12_out);
  _7_Segment_Display #(.active("false"), .decimalPoint("false")) H0 (
    .g(H0_Count_0_9_pin14), .f(H0_Count_0_9_pin15), .a(H0_Count_0_9_pin13), .b(H0_Count_0_9_pin12),
    .e(H0_Count_0_9_pin9), .d(H0_Count_0_9_pin10), .c(H0_Count_0_9_pin11));
  and and_7 (and_7_out, UP_H0, Time_Set);
  not not_14 (not_14_out, H0_Counter_carry);
  not not_15 (not_15_out, Pause_Stopwatch);
  Counter #(.max('h5), .width(4)) M1_Stopwatch_Counter (
    .clr(or_2_out), .clk(not_18_out), .Q(M1_Stopwatch_Counter_q));  // open: load, up, count, D, carry
  and and_8 (CLK_Stopwatch, and_5_out, not_15_out);
  Multiplexer #(.width(4)) multiplexer_4 (
    .in0(M1_Clk_Out), .in1(M1_Stopwatch_Counter_q), .out(M1_Input), .sel(Stopwatch_Mode));
  _7447 #(.ShowInternalStructure("true")) M1_Count_0_5 (
    .pin1(M1_Input[1]), .pin2(M1_Input[2]), .pin3(M1_Count_0_5_pin3), .pin5(M1_Count_0_5_pin3),
    .pin6(M1_Input[3]), .pin7(M1_Input[0]), .pin15(M1_Count_0_5_pin15), .pin14(M1_Count_0_5_pin14),
    .pin13(M1_Count_0_5_pin13), .pin12(M1_Count_0_5_pin12), .pin11(M1_Count_0_5_pin11),
    .pin10(M1_Count_0_5_pin10), .pin9(M1_Count_0_5_pin9));  // open: pin4
  Counter #(.max('h5), .width(4)) M1_Counter (
    .clr(or_1_out), .clk(not_19_out), .carry(M1_Counter_carry), .Q(M1_Clk_Out));  // open: load, up, count, D
  _7_Segment_Display #(.active("false"), .decimalPoint("false")) M1 (
    .g(M1_Count_0_5_pin14), .f(M1_Count_0_5_pin15), .a(M1_Count_0_5_pin13), .b(M1_Count_0_5_pin12),
    .e(M1_Count_0_5_pin9), .d(M1_Count_0_5_pin10), .c(M1_Count_0_5_pin11));
  Counter #(.max('h9), .width(4)) M0_Stopwatch_Counter (
    .clr(or_2_out), .clk(not_20_out), .carry(M0_Stopwatch_Counter_carry), .Q(M0_Stopwatch_Counter_q));  // open: load, up, count, D
  not not_16 (not_16_out, M1_Counter_carry);
  Multiplexer #(.width(4)) multiplexer_5 (
    .in0(M0_Clk_Out), .in1(M0_Stopwatch_Counter_q), .out(M0_Input), .sel(Stopwatch_Mode));
  _7447 #(.ShowInternalStructure("true")) MO_Count_0_9 (
    .pin1(M0_Input[1]), .pin2(M0_Input[2]), .pin3(MO_Count_0_9_pin3), .pin4(MO_Count_0_9_pin3),
    .pin5(MO_Count_0_9_pin3), .pin6(M0_Input[3]), .pin7(M0_Input[0]), .pin15(MO_Count_0_9_pin15),
    .pin14(MO_Count_0_9_pin14), .pin13(MO_Count_0_9_pin13), .pin12(MO_Count_0_9_pin12),
    .pin11(MO_Count_0_9_pin11), .pin10(MO_Count_0_9_pin10), .pin9(MO_Count_0_9_pin9));
  Counter #(.max('h9), .width(4)) MO_Counter (
    .clr(or_1_out), .clk(and_9_out), .carry(MO_Counter_carry), .Q(M0_Clk_Out));  // open: load, up, count, D
  and and_9 (and_9_out, not_21_out, not_17_out);
  _7_Segment_Display #(.active("false"), .decimalPoint("false")) MO (
    .g(MO_Count_0_9_pin14), .f(MO_Count_0_9_pin15), .a(MO_Count_0_9_pin13), .b(MO_Count_0_9_pin12),
    .e(MO_Count_0_9_pin9), .d(MO_Count_0_9_pin10), .c(MO_Count_0_9_pin11));
  not not_17 (not_17_out, and_10_out);
  and and_10 (and_10_out, UP_M0, Time_Set);
  not not_18 (not_18_out, M0_Stopwatch_Counter_carry);
  DipSwitch #(.number(6)) dipswitch_1 (
    .sw1(Pause_Clock), .sw2(Manual_Reset_Clock), .sw3(Stopwatch_Mode), .sw4(Pause_Stopwatch),
    .sw5(Reset_Stopwatch), .sw6(Time_Set));
  not not_19 (not_19_out, MO_Counter_carry);
  Counter #(.max('h5), .width(4)) S1_Stopwatch_Counter (
    .clr(or_2_out), .clk(not_23_out), .carry(S1_Stopwatch_Counter_carry), .Q(S1_Stopwatch_Counter_q));  // open: load, up, count, D
  Counter #(.max('h5), .width(4)) S1_Counter (
    .clr(or_1_out), .clk(not_22_out), .carry(S1_Counter_carry), .Q(S1_Clk_Out));  // open: load, up, count, D
  Multiplexer #(.width(4)) multiplexer_6 (
    .in0(S1_Clk_Out), .in1(S1_Stopwatch_Counter_q), .out(S1_Input), .sel(Stopwatch_Mode));
  _7_Segment_Display #(.active("false"), .decimalPoint("false")) S1 (
    .g(S1_Count_0_5_pin14), .f(S1_Count_0_5_pin15), .a(S1_Count_0_5_pin13), .b(S1_Count_0_5_pin12),
    .e(S1_Count_0_5_pin9), .d(S1_Count_0_5_pin10), .c(S1_Count_0_5_pin11));
  _7447 #(.ShowInternalStructure("true")) S1_Count_0_5 (
    .pin1(S1_Input[1]), .pin2(S1_Input[2]), .pin3(S1_Count_0_5_pin3), .pin4(S1_Count_0_5_pin3),
    .pin5(S1_Count_0_5_pin3), .pin6(S1_Input[3]), .pin7(S1_Input[0]), .pin15(S1_Count_0_5_pin15),
    .pin14(S1_Count_0_5_pin14), .pin13(S1_Count_0_5_pin13), .pin12(S1_Count_0_5_pin12),
    .pin11(S1_Count_0_5_pin11), .pin10(S1_Count_0_5_pin10), .pin9(S1_Count_0_5_pin9));
  not not_20 (not_20_out, S1_Stopwatch_Counter_carry);
  not not_21 (not_21_out, S1_Counter_carry);
  _7447 #(.ShowInternalStructure("true")) S0_Count_0_9 (
    .pin1(S0_Input[1]), .pin2(S0_Input[2]), .pin3(S0_Count_0_9_pin3), .pin4(S0_Count_0_9_pin3),
    .pin5(S0_Count_0_9_pin3), .pin6(S0_Input[3]), .pin7(S0_Input[0]), .pin15(S0_Count_0_9_pin15),
    .pin14(S0_Count_0_9_pin14), .pin13(S0_Count_0_9_pin13), .pin12(S0_Count_0_9_pin12),
    .pin11(S0_Count_0_9_pin11), .pin10(S0_Count_0_9_pin10), .pin9(S0_Count_0_9_pin9));
  Counter #(.max('h9), .width(4)) S0_Counter (
    .clr(or_1_out), .clk(CLK), .carry(S0_Counter_carry), .Q(S0_Clk_Out));  // open: load, up, count, D
  Counter #(.max('h9), .width(4)) S0_Stopwatch_Counter (
    .clr(or_2_out), .clk(CLK_Stopwatch), .carry(S0_Stopwatch_Counter_carry), .Q(S0_Stopwatch_Counter_q));  // open: load, up, count, D
  _7_Segment_Display #(.active("false"), .decimalPoint("false")) S0 (
    .g(S0_Count_0_9_pin14), .f(S0_Count_0_9_pin15), .a(S0_Count_0_9_pin13), .b(S0_Count_0_9_pin12),
    .e(S0_Count_0_9_pin9), .d(S0_Count_0_9_pin10), .c(S0_Count_0_9_pin11));
  Multiplexer #(.width(4)) multiplexer_7 (
    .in0(S0_Clk_Out), .in1(S0_Stopwatch_Counter_q), .out(S0_Input), .sel(Stopwatch_Mode));
  not not_22 (not_22_out, S0_Counter_carry);
  not not_23 (not_23_out, S0_Stopwatch_Counter_carry);
  Button u_UP_H0 (.out(UP_H0));
  Button u_UP_M0 (.out(UP_M0));
  // also tied to VCC on the sheet: {H1_Count_0_2_pin3, H0_Count_0_9_pin3, M1_Count_0_5_pin3, MO_Count_0_9_pin3, S1_Count_0_5_pin3, S0_Count_0_9_pin3}

  // Other names for the same wires on the sheet: H0_Input[2] = H0_4; H1_Input[1] = H1_2

  // Notes on the sheet:
  //   Components
  //   Ignore
  //   Reset Stopwatch when Not Using
  //   Reset at 24:00:00
  //   Hours
  //   Time Set | Pause Digital Clock | Start & Pause Stopwatch
  //   :
  //   Stopwatch (MM:SS)
  //   24-Hour Digital Clock (HH:MM:SS)
  //   Minutes
  //   :
  //   DIP Switch
  //   Seconds
  //   Time Set Features
endmodule
