// Logisim project Project_1_Circuit.circ as structural Verilog: 2 circuits, main circuit Project1
module Project1 (
  input  A,
  input  B,
  input  C,
  input  D,
  output R1,
  output G1,
  output R2,
  output G2,
  output R3,
  output G3,
  output R4,
  output G4
);

  wire and_1_out, and_2_out, and_3_out, and_4_out, and_5_out, and_6_out, and_7_out, not_1_out, not_2_out,
       not_3_out, not_4_out, not_5_out, or_1_out, or_2_out, xor_1_out, xor_2_out, xor_3_out;

  not not_1 (not_1_out, A);
  not not_2 (not_2_out, B);
  not not_3 (not_3_out, C);
  not not_4 (not_4_out, D);
  and and_1 (and_1_out, C, B);
  xor xor_1 (xor_1_out, C, D);
  and and_2 (and_2_out, not_3_out, not_4_out);
  and and_3 (and_3_out, not_2_out, C, D);
  or or_1 (or_1_out, not_2_out, C);
  or or_2 (or_2_out, not_3_out, not_4_out);
  xor xor_2 (xor_2_out, B, D);
  xor xor_3 (xor_3_out, C, D);
  and and_4 (and_4_out, B, not_3_out);
  and and_5 (and_5_out, C, D);
  and and_6 (and_6_out, C, B);
  or or_3 (R1, and_1_out, xor_1_out);
  or or_4 (G1, and_2_out, and_3_out);
  and and_7 (and_7_out, D, or_1_out);
  and and_8 (G2, B, or_2_out);
  and and_9 (R3, not_1_out, xor_2_out, xor_3_out);
  or or_5 (G3, and_4_out, and_5_out);
  not not_5 (not_5_out, and_6_out);
  or or_6 (R2, A, and_7_out);
  and and_10 (R4, not_1_out, D, not_5_out);

  assign G4 = 1'b0;
endmodule

module NANDOnly (
  input  A,
  input  B,
  input  C,
  input  D,
  output R1,
  output G1
);

  wire nand_1_out, nand_2_out, nand_3_out, nand_4_out, nand_5_out, nand_6_out, nand_7_out, nand_8_out,
       nand_9_out, nand_10_out, nand_11_out, nand_12_out;

  nand nand_1 (nand_1_out, B, B);
  nand nand_2 (nand_2_out, C, C);
  nand nand_3 (nand_3_out, D, D);
  nand nand_4 (nand_4_out, C, nand_3_out);
  nand nand_5 (nand_5_out, C, B);
  nand nand_6 (nand_6_out, nand_1_out, C);
  nand nand_7 (nand_7_out, nand_4_out, nand_5_out);
  nand nand_8 (nand_8_out, nand_6_out, nand_6_out);
  nand nand_9 (nand_9_out, nand_7_out, nand_7_out);
  nand nand_10 (nand_10_out, nand_2_out, D);
  nand nand_11 (nand_11_out, nand_2_out, nand_3_out);
  nand nand_12 (nand_12_out, nand_8_out, D);
  nand nand_13 (R1, nand_9_out, nand_10_out);
  nand nand_14 (G1, nand_11_out, nand_12_out);
endmodule
