// Logisim project Project_2_Circuit.circ as structural Verilog: 2 circuits, main circuit main
module main (
);

  vending_machine vending_machine_1 ();  // open: D_25_1, E_50_2, CLK_Pause_3, Reset_4
endmodule

module vending_machine (
  input  D_25_1,
  input  E_50_2,
  input  CLK_Pause_3,
  input  Reset_4
);

  wire and_1_out, and_2_out, and_3_out, and_4_out, and_5_out, and_6_out, and_7_out, and_8_out, and_9_out,
       and_10_out, and_11_out, and_12_out, and_13_out, and_14_out, and_15_out, and_16_out, and_17_out,
       and_18_out, ANOT_B_out, C_D_ENOT_out, CDE_OR_DE_out, clock_1_out, D_NOT_out, D_XOR_E_out, Da_q, Da_qn,
       Db_q, Db_qn, Dc_q, Dc_qn, DNOT_E_out, E_NOT_out, n7447_1_pin2, n7447_1_pin3, n7447_1_pin9,
       n7447_1_pin10, n7447_1_pin11, n7447_1_pin12, n7447_1_pin13, n7447_1_pin14, n7447_1_pin15,
       n7447_2_pin3, n7447_2_pin9, n7447_2_pin10, n7447_2_pin11, n7447_2_pin12, n7447_2_pin13, n7447_2_pin14,
       n7447_2_pin15, not_1_out, not_2_out, or_1_out, or_2_out, or_3_out, or_4_out, or_5_out, or_6_out,
       or_7_out, or_8_out, xor_1_out;

  not D_NOT (D_NOT_out, D_25_1);
  not E_NOT (E_NOT_out, E_50_2);
  and ANOT_B (ANOT_B_out, Da_qn, Db_q);
  and DNOT_E (DNOT_E_out, D_NOT_out, E_50_2);
  and C_D_ENOT (C_D_ENOT_out, Dc_q, D_25_1, E_NOT_out);
  or CDE_OR_DE (CDE_OR_DE_out, DNOT_E_out, C_D_ENOT_out);
  xor D_XOR_E (D_XOR_E_out, D_25_1, E_50_2);
  and and_1 (and_1_out, Dc_qn, E_NOT_out);
  not not_1 (not_1_out, D_XOR_E_out);
  and and_2 (and_2_out, Db_qn, D_NOT_out);
  and and_3 (and_3_out, D_25_1, E_50_2);
  or or_1 (or_1_out, and_1_out, not_1_out);
  xor xor_1 (xor_1_out, Dc_q, D_25_1);
  or or_2 (or_2_out, and_2_out, and_3_out);
  or or_3 (or_3_out, DNOT_E_out, Db_q);
  and and_4 (and_4_out, ANOT_B_out, Dc_q, DNOT_E_out);
  and and_5 (and_5_out, Db_qn, CDE_OR_DE_out);
  and and_6 (and_6_out, Db_q, or_1_out);
  and and_7 (and_7_out, E_NOT_out, xor_1_out);
  and and_8 (and_8_out, Dc_q, or_2_out);
  or or_4 (or_4_out, CDE_OR_DE_out, Db_q);
  and and_9 (and_9_out, Dc_q, or_3_out);
  or or_5 (or_5_out, and_9_out, and_10_out);
  and and_10 (and_10_out, Db_q, D_XOR_E_out);
  _7447 #(.ShowInternalStructure("true")) u_7447_1 (
    .pin1(and_4_out), .pin2(n7447_1_pin2), .pin3(n7447_1_pin3), .pin4(n7447_1_pin3), .pin5(n7447_1_pin3),
    .pin6(n7447_1_pin2), .pin7(n7447_1_pin2), .pin15(n7447_1_pin15), .pin14(n7447_1_pin14),
    .pin13(n7447_1_pin13), .pin12(n7447_1_pin12), .pin11(n7447_1_pin11), .pin10(n7447_1_pin10),
    .pin9(n7447_1_pin9));
  or or_6 (or_6_out, and_5_out, and_6_out);
  and and_11 (and_11_out, Da_qn, or_7_out);
  or or_7 (or_7_out, and_7_out, and_8_out);
  and and_12 (and_12_out, Da_qn, or_8_out);
  or or_8 (or_8_out, D_XOR_E_out, Dc_q, Db_q, 1'b0);
  and and_13 (and_13_out, Da_qn, or_4_out);
  and and_14 (and_14_out, Da_qn, or_5_out);
  and and_15 (and_15_out, ANOT_B_out, CDE_OR_DE_out);
  and and_16 (and_16_out, Da_qn, or_6_out);
  and and_17 (and_17_out, ANOT_B_out, CDE_OR_DE_out);
  _7_Segment_Display #(.active("false"), .decimalPoint("false")) u_7_segment_display_1 (
    .g(n7447_1_pin14), .f(n7447_1_pin15), .a(n7447_1_pin13), .b(n7447_1_pin12), .e(n7447_1_pin9),
    .d(n7447_1_pin10), .c(n7447_1_pin11));
  Clock clock_1 (.out(clock_1_out));
  not not_2 (not_2_out, CLK_Pause_3);
  and and_18 (and_18_out, not_2_out, clock_1_out);
  _7447 #(.ShowInternalStructure("true")) u_7447_2 (
    .pin1(n7447_1_pin2), .pin2(and_4_out), .pin3(n7447_2_pin3), .pin4(n7447_2_pin3), .pin5(n7447_2_pin3),
    .pin6(n7447_1_pin2), .pin7(n7447_1_pin2), .pin15(n7447_2_pin15), .pin14(n7447_2_pin14),
    .pin13(n7447_2_pin13), .pin12(n7447_2_pin12), .pin11(n7447_2_pin11), .pin10(n7447_2_pin10),
    .pin9(n7447_2_pin9));
  D_Flip_Flop Da (.D(and_15_out), .clk(and_18_out), .Q(Da_q), .Qn(Da_qn), .preset(1'b0), .reset(Reset_4));
  D_Flip_Flop Db (.D(and_16_out), .clk(and_18_out), .Q(Db_q), .Qn(Db_qn), .preset(1'b0), .reset(Reset_4));
  D_Flip_Flop Dc (.D(and_11_out), .clk(and_18_out), .Q(Dc_q), .Qn(Dc_qn), .preset(1'b0), .reset(Reset_4));
  LED R1 (.in(1'b1));
  // RGBLED R1G1: pin names not known; wires that end beside it: 1'b1, and_12_out
  LED G1 (.in(and_12_out));
  LED R2 (.in(and_13_out));
  // RGBLED R2G2: pin names not known; wires that end beside it: and_13_out, and_14_out
  LED G2 (.in(and_14_out));
  LED R3 (.in(and_17_out));
  _7_Segment_Display #(.active("false"), .decimalPoint("false")) u_7_segment_display_2 (
    .g(n7447_2_pin14), .f(n7447_2_pin15), .a(n7447_2_pin13), .b(n7447_2_pin12), .e(n7447_2_pin9),
    .d(n7447_2_pin10), .c(n7447_2_pin11));
  // also tied to GND on the sheet: n7447_1_pin2
  // also tied to VCC on the sheet: {n7447_1_pin3, n7447_2_pin3}
endmodule
